# Fritzing sketch bt (saved by Fritzing 0.9.3b)
breadboards: 1

parts:
  Part1 = Arduino Uno (Rev3) - ICSP
  J1 = Basic Servo
  Part2 = Bluetooth HC-05 Macho

nets:
  N1: Part1.D10_PWM/SS, J1.pulse
  N2: Part1.D0/RX, Part2.TXD
  N3: Part1.D1/TX, Part2.RXD
  5V: Part1.5V, Part2.VCC
  GND: Part1.GND, Part2.GND

notes:
  Warning:
  When tx and rx are connected to the HC05, the usb cannot load programs to the arduino board.
