# Fritzing sketch knock (saved by Fritzing 0.9.3b)
breadboards: 1

parts:
  Part1 = Arduino Uno (Rev3) - ICSP
  J1 = Basic Servo
  S1 = Pushbutton [package="[THT]"]
  J2 = Piezo Speaker
  J3 = Piezo Speaker
  R1 = Resistor [tolerance=±5% resistance=1M package=THT]

nets:
  N1: Part1.A0, J3.pin1
  N2: Part1.D3_PWM, J2.pin2
  N3: Part1.D4, J1.pulse
  N4: Part1.D5_PWM, S1.Pin_3, S1.Pin_4
  5V: Part1.5V, J1.vcc
  GND: Part1.GND, J1.gnd, S1.Pin_1, S1.Pin_2, J2.pin1, R1.Pin_0

notes:
  This is a passive buzzer. Which'll listen to knocks.
  This is an active buzzer. Which'll inform the state.

custom parts:
  Piezo Speaker: Piezo
