# Fritzing sketch sniffer (saved by Fritzing 0.9.3b)
breadboards: 1

parts:
  Part1 = Arduino Uno (Rev3) - ICSP
  IR1 = TSOP312.., 314.. [package=THT]
  R1 = Resistor [tolerance=±5% resistance=220 package="1206 [SMD]"]
  DI1 = 7-Segment LED Display [package=THT]

nets:
  N1: Part1.D8, DI1.cathodeC
  N2: Part1.D9_PWM, DI1.cathodeA
  N3: Part1.D10_PWM/SS, DI1.cathodeB
  N4: Part1.D2, IR1.GND
  N5: Part1.D4, DI1.cathodeG
  N6: Part1.D5_PWM, DI1.cathodeF
  N7: Part1.D6_PWM, DI1.cathodeE
  N8: Part1.D7, DI1.cathodeD
  N9: Part1.5V, IR1.Data, R1.Pin_0
  N10: Part1.GND, IR1.Vs
  N11: R1.Pin_1, DI1.commAnode#7
