# Fritzing sketch tester (saved by Fritzing 0.9.3b)
breadboards: 1

parts:
  Part1 = Arduino Uno (Rev3) - ICSP
  J2 = Piezo Speaker
  LED1 = smd LED [color="Infrared (940nm)" package="0603 [SMD]"]
  R1 = Resistor [tolerance=±5% resistance=220 package="1206 [SMD]"]

nets:
  N1: Part1.D3_PWM, J2.pin2
  N2: Part1.D5_PWM, R1.Pin_1
  N3: Part1.GND, J2.pin1, LED1.cathode
  N4: LED1.anode, R1.Pin_0

custom parts:
  Piezo Speaker: Piezo
