# Fritzing sketch rfid (saved by Fritzing 0.9.3b)
circuit board: 8.46667cm x 5.64444cm
breadboards: 1

parts:
  Componente1 = RFID-RC522-v2
  R2 = Resistor [tolerance=±5% resistance=220 package=THT]  # not connected
  Part1 = Arduino Uno (Rev3) - ICSP
  S1 = Momentary Switch [package=ksa_sealed_tac_switch]
  LED1 = smd LED [color="Green (555nm)" package="1206 [SMD]"]
  LED2 = smd LED [color="Red (633nm)" package="1206 [SMD]"]
  LED3 = smd LED [color="Blue (430nm)" package="1206 [SMD]"]
  R3 = Resistor [tolerance=±5% resistance=220 package="2010 [SMD]"]
  R4 = Resistor [tolerance=±5% resistance=220 package="2010 [SMD]"]
  R5 = Resistor [tolerance=±5% resistance=220 package="2010 [SMD]"]
  J1 = Basic Servo

nets:
  N1: Componente1.SDA, Part1.D10_PWM/SS
  N2: Componente1.SCK, Part1.D13/SCK
  N3: Componente1.MOSI, Part1.D11_PWM/MOSI
  N4: Componente1.MISO, Part1.ICSP_MISO, Part1.D12/MISO
  GND: Componente1.GND, Part1.GND, S1.1, R3.Pin_0, R4.Pin_0, R5.Pin_0
  N5: Componente1.RST, Part1.D9_PWM
  3.3V: Componente1.3.3V, Part1.3V3
  N6: Part1.D8, J1.pulse
  N7: Part1.D3_PWM, S1.3
  N8: Part1.D5_PWM, LED3.anode
  N9: Part1.D6_PWM, LED2.anode
  N10: Part1.D7, LED1.anode
  N11: LED1.cathode, R4.Pin_1
  N12: LED2.cathode, R5.Pin_1
  N13: LED3.cathode, R3.Pin_1

custom parts:
  RFID-RC522-v2: A simple China made RFID-RC522 Reader; do check the pin labels, as this is a MFRC522 based clone.

// code stored in the sketch: Untitled2.ino
/*
 * 
 * All the resources for this project: http://randomnerdtutorials.com/
 * Modified by José Vicente
 * 
 * Created by Japtech
 * 
 */
 
#include <SPI.h>
#include <MFRC522.h>
#include <LiquidCrystal.h>
 
#define SS_PIN 53
#define RST_PIN 6
LiquidCrystal lcd(12, 11, 5, 4, 3, 2);

MFRC522 mfrc522(SS_PIN, RST_PIN);   // Create MFRC522 instance.

void setup() 
{
  lcd.begin(16, 2);
  pinMode(7, OUTPUT);
  pinMode(8, OUTPUT);
  Serial.begin(9600);   // Initiate a serial communication
  SPI.begin();      // Initiate  SPI bus
  mfrc522.PCD_Init();   // Initiate MFRC522
  Serial.println("Approximate your card to the reader...");
  Serial.println();
  lcd.print("waiting for card");
}
void loop() 
{
  // Look for new cards
  
  if ( ! mfrc522.PICC_IsNewCardPresent()) 
  {
    return;
  }
  // Select one of the cards
  if ( ! mfrc522.PICC_ReadCardSerial()) 
  {
    return;
  }
  //Show UID on serial monitor
  Serial.print("UID tag :");
  String content= "";
  byte letter;
  for (byte i = 0; i < mfrc522.uid.size; i++) 
  {
     Serial.print(mfrc522.uid.uidByte[i] < 0x10 ? " 0" : " ");
     Serial.print(mfrc522.uid.uidByte[i], HEX);
         
     content.concat(String(mfrc522.uid.uidByte[i] < 0x10 ? " 0" : " "));
     content.concat(String(mfrc522.uid.uidByte[i], HEX));
  }
  Serial.println();
  Serial.print("Message : ");
  content.toUpperCase();
  if (content.substring(1) == "63 8C E5 C7") //change here the UID of the card/cards that you want to give access
  {
    Serial.println("Authorized access");
    lcd.clear();
    lcd.print("Authorized access");
    digitalWrite(7, HIGH);
    delay(3000);
    digitalWrite(7, LOW);
    lcd.clear();
    lcd.print("waiting for card");
    Serial.println();
  }
 
 else   {
    Serial.println(" Access denied");
    lcd.clear();
    lcd.print(" Access denied");
    digitalWrite(8, HIGH);
    delay(3000);
    digitalWrite(8, LOW);
    lcd.clear();
    lcd.print("waiting for card");
  }
}
