# Fritzing sketch anticat (saved by Fritzing 0.9.3b)
breadboards: 1

parts:
  Part1 = Arduino Uno (Rev3)
  hc-sr2 = hc-sr04
  J1 = Basic Servo
  LED1 = LED - 5mm [color="Red (633nm)" package="5 mm [THT]"]
  LED2 = LED - 5mm [color="Green (565nm)" package="5 mm [THT]"]
  J2 = Piezo Speaker
  R2 = Resistor [tolerance=±5% resistance=220 package=THT]
  R3 = Resistor [tolerance=±5% resistance=220 package=THT]

nets:
  N1: Part1.D8, hc-sr2.Echo
  N2: Part1.D9_PWM, J1.pulse
  GND: Part1.GND, hc-sr2.GND, J1.gnd, LED1.cathode, J2.pin1
  N3: Part1.D2, J2.pin2
  N4: Part1.D3_PWM, R2.Pin_1
  N5: Part1.D4, R3.Pin_1
  N6: Part1.D7, hc-sr2.Trig
  VCC: Part1.5V, hc-sr2.VCC, J1.vcc
  N7: LED1.anode, R3.Pin_0
  N8: LED2.anode, R2.Pin_0

custom parts:
  Piezo Speaker: Piezo
