# Fritzing sketch laser3 (saved by Fritzing 0.9.3b)
breadboards: 1

parts:
  Part1 = Arduino Uno (Rev3) - ICSP
  R2 = Resistor [tolerance=±5% resistance=10k package="2010 [SMD]"]
  Part2 = Humidity Sensor - HIH-4030 Breakout [part_number="well... laser !"]
  J1 = Piezo Speaker
  R3 = PHOTOCELL [package=photocell]
  R4 = Resistor [tolerance=±5% resistance=220 package="2010 [SMD]"]
  R5 = Resistor [tolerance=±5% resistance=220 package="2010 [SMD]"]
  R6 = Resistor [tolerance=±5% resistance=220 package="2010 [SMD]"]
  LED1 = LED - 5mm [color="Green (565nm)" package="5 mm [THT]"]
  LED2 = LED - 5mm [color="Yellow (595nm)" package="5 mm [THT]"]
  LED3 = LED - 5mm [color="Red (633nm)" package="5 mm [THT]"]
  S1 = Round Pushbutton
  J2 = Basic Servo
  U1 = POT [package=pot_mammoth]
  U2 = POT [package=pot_mammoth]
  J3 = Basic Servo

nets:
  N1: Part1.A0, R2.Pin_1, R3.P$1
  N2: Part1.A1, U1.A
  N3: Part1.A2, U2.A
  N4: Part1.D8, J1.pin2
  N5: Part1.D10_PWM/SS, Part2.VCC
  N6: Part1.D11_PWM/MOSI, J3.pulse
  N7: Part1.D12/MISO, J2.pulse
  N8: Part1.D2, S1.leg0
  N9: Part1.D4, LED1.anode
  N10: Part1.D5_PWM, LED2.anode
  N11: Part1.D6_PWM, LED3.anode
  5V: Part1.5V, R3.P$2, U1.S, U2.S, J3.vcc
  GND: Part1.GND, R2.Pin_0, Part2.GND, J1.pin1, R4.Pin_0, R5.Pin_0, R6.Pin_0, S1.leg1, J2.gnd, U1.E, U2.E, J3.gnd
  N12: R4.Pin_1, LED1.cathode
  N13: R5.Pin_1, LED2.cathode
  N14: R6.Pin_1, LED3.cathode

custom parts:
  Piezo Speaker: Piezo

// code stored in the sketch: shift.ino
/*
  Shift Register Example
 for 74HC595 shift register

 This sketch turns reads serial input and uses it to set the pins
 of a 74HC595 shift register.

 Hardware:
 * 74HC595 shift register attached to pins 2, 3, and 4 of the Arduino,
 as detailed below.
 * LEDs attached to each of the outputs of the shift register

 Created 22 May 2009
 Created 23 Mar 2010
 by Tom Igoe

 */

//Pin connected to latch pin (ST_CP) of 74HC595
const int latchPin = 8;
//Pin connected to clock pin (SH_CP) of 74HC595
const int clockPin = 12;
////Pin connected to Data in (DS) of 74HC595
const int dataPin = 11;

void setup() {
  //set pins to output because they are addressed in the main loop
  pinMode(latchPin, OUTPUT);
  pinMode(dataPin, OUTPUT);  
  pinMode(clockPin, OUTPUT);
  
}
int hamten = 0; 

void loop()
{
//  registerWrite(255);
 
registerWrite(~1);
registerWrite(~9);
registerWrite(~13);
registerWrite(~15);
registerWrite(~47);
registerWrite(~111);
registerWrite(~239);
registerWrite(~239);
registerWrite(~111);
registerWrite(~47);
registerWrite(~15);
registerWrite(~13);
registerWrite(~9);
registerWrite(~1);
registerWrite(~1);


}

// This method sends bits to the shift register:

void registerWrite(int bitsToSend) {
  digitalWrite(latchPin, LOW);
   digitalWrite(clockPin, LOW);
  shiftOut(dataPin, clockPin, MSBFIRST, bitsToSend);
  digitalWrite(latchPin, HIGH);
  hamten = analogRead(0);
   delay(hamten);
}
