# Fritzing sketch lcd (saved by Fritzing 0.9.3b)
breadboards: 1

parts:
  Part1 = Arduino Leonardo (Rev3b)
  LCD1 = LCD screen
  R1 = Resistor [tolerance=±5% resistance=220 package="0603 [SMD]"]
  R2 = Resistor [tolerance=±5% resistance=220 package="0603 [SMD]"]

nets:
  N1: Part1.D3_PWM/SCL, LCD1.DB6
  N2: Part1.D4/A6, LCD1.DB5
  N3: Part1.D6_PWM/A7, LCD1.DB7
  5V: Part1.5V, LCD1.VDD, R1.Pin_0
  N4: Part1.D11_PWM, LCD1.E
  N5: Part1.D12/A11, LCD1.RS
  GND: Part1.GND, LCD1.VSS, LCD1.R/W, LCD1.LED-, R2.Pin_0
  N6: LCD1.V0, R2.Pin_1
  N7: LCD1.LED+, R1.Pin_1
