# Fritzing sketch motor (saved by Fritzing 0.9.3b)
breadboards: 1

parts:
  R1 = Resistor [tolerance=±5% resistance=220 package="0805 [SMD]"]  # not connected
  Part1 = Arduino Uno (Rev3) - ICSP
  M1 = DC Motor
  VCC1 = 4 x AAA Battery Mount
  IC1 = L293D [package=THT]

nets:
  N1: Part1.D9_PWM, IC1.In_2
  N2: Part1.D10_PWM/SS, IC1.In_1
  N3: Part1.D11_PWM/MOSI, IC1.Enable_1
  N4: Part1.5V, IC1.+V
  N5: Part1.GND, VCC1.-, IC1.0V
  N6: M1.pin_1, IC1.Out_1_(_Controlled_by_Enable_1_)
  N7: M1.pin_2, IC1.Out_2_(_Controlled_by_Enable_1_)
  N8: VCC1.+, IC1.+Vmotor
