# Fritzing sketch read_ir (saved by Fritzing 0.9.3b)
breadboards: 1

parts:
  Part1 = Arduino Uno (Rev3) - ICSP
  IR1 = TSOP312.., 314.. [package=THT]
  J1 = Basic Servo

nets:
  N1: Part1.D2, IR1.GND
  N2: Part1.D4, J1.pulse
  5V: Part1.5V, IR1.Data, J1.vcc
  GND: Part1.GND, IR1.Vs, J1.gnd
