# Fritzing sketch sendmult (saved by Fritzing 0.9.3b)
breadboards: 1

parts:
  Part1 = Arduino Uno (Rev3) - ICSP
  R1 = Resistor [tolerance=±5% resistance=220 package="2010 [SMD]"]
  7_Segment1 = 7 Segment Display  # not connected
  LED1 = smd LED [color="Red (633nm)" package="0603 [SMD]"]
  S1 = Momentary Switch [package=ksa_sealed_tac_switch]
  S3 = Momentary Switch [package=ksa_sealed_tac_switch]
  R2 = Resistor [tolerance=±5% resistance=220 package="2010 [SMD]"]
  R3 = Resistor [tolerance=±5% resistance=220 package="2010 [SMD]"]

nets:
  N1: Part1.D3_PWM, LED1.anode
  N2: Part1.D4, S3.1, R3.Pin_0
  N3: Part1.D5_PWM, S1.1, R2.Pin_0
  N4: Part1.5V, R1.Pin_0, S1.3, S3.3
  N5: Part1.GND, LED1.cathode, R2.Pin_1, R3.Pin_1

notes:
  1= lower left
  7
  -----
  9 | | 6
  --10-
  1 | | 4
  -----
  2 .5
