# Fritzing sketch shift (saved by Fritzing 0.9.3b)
breadboards: 1

parts:
  R1 = Rotary Potentiometer (Large) [maximum_resistance=100kΩ package=THT]  # not connected
  U1 = 74HC595 [package="DIP16 [THT]"]
  7_Segment2 = 7 Segment Display
  Part1 = Arduino Uno (Rev3) - ICSP
  R2 = Resistor [tolerance=±5% resistance=220 package="2010 [SMD]"]
  U2 = 74HC595 [package="DIP16 [THT]"]  # not connected
  7_Segment3 = 7 Segment Display  # not connected

nets:
  N1: U1.Q1, 7_Segment2.Segment_E
  N2: U1.Q2, 7_Segment2.Segment_D
  N3: U1.Q3, 7_Segment2.Segment_C
  N4: U1.Q4, 7_Segment2.Segment_DP
  N5: U1.Q5, 7_Segment2.Segment_B
  N6: U1.Q6, 7_Segment2.Segment_A
  N7: U1.Q7, 7_Segment2.Segment_F
  GND: U1.GND, U1.OE, Part1.GND
  VCC: U1.MR, U1.VCC, Part1.5V, R2.Pin_0
  N8: U1.SH_CP, Part1.D12/MISO
  N9: U1.ST_CP, Part1.D8
  N10: U1.DS, Part1.D11_PWM/MOSI
  N11: U1.Q0, 7_Segment2.Segment_G
  N12: 7_Segment2.common_anode, R2.Pin_1

notes:
  1 is lower left
  GND (pin 8) to ground
  Vcc (pin 16) to 5V
  OE (pin 13) to ground
  MR (pin 10) to 5V
  DS (pin 14) to DigitalPin 11
  SH_CP (pin 11) DigitalPin 12
  ST_CP (pin 12) DigitalPin 8
  pin 15 = 1
  Pin 1..7 = 2..8
  Pin 9 = 9
  1= lower left
  7
  -----
  9 | | 6
  --10-
  1 | | 4
  -----
  2 .5
  1= lower left
  7
  -----
  8 | | 6
  --1--
  2 | | 4
  -----
  3 .5

// code stored in the sketch: shift.ino
/*
  Shift Register Example
 for 74HC595 shift register

 This sketch turns reads serial input and uses it to set the pins
 of a 74HC595 shift register.

 Hardware:
 * 74HC595 shift register attached to pins 2, 3, and 4 of the Arduino,
 as detailed below.
 * LEDs attached to each of the outputs of the shift register

 Created 22 May 2009
 Created 23 Mar 2010
 by Tom Igoe

 */

//Pin connected to latch pin (ST_CP) of 74HC595
const int latchPin = 8;
//Pin connected to clock pin (SH_CP) of 74HC595
const int clockPin = 12;
////Pin connected to Data in (DS) of 74HC595
const int dataPin = 11;

void setup() {
  //set pins to output because they are addressed in the main loop
  pinMode(latchPin, OUTPUT);
  pinMode(dataPin, OUTPUT);  
  pinMode(clockPin, OUTPUT);
  
}
int hamten = 0; 

void loop()
{
//  registerWrite(255);
 
registerWrite(~1);
registerWrite(~9);
registerWrite(~13);
registerWrite(~15);
registerWrite(~47);
registerWrite(~111);
registerWrite(~239);
registerWrite(~239);
registerWrite(~111);
registerWrite(~47);
registerWrite(~15);
registerWrite(~13);
registerWrite(~9);
registerWrite(~1);
registerWrite(~1);


}

// This method sends bits to the shift register:

void registerWrite(int bitsToSend) {
  digitalWrite(latchPin, LOW);
   digitalWrite(clockPin, LOW);
  shiftOut(dataPin, clockPin, MSBFIRST, bitsToSend);
  digitalWrite(latchPin, HIGH);
  hamten = analogRead(0);
   delay(hamten);
}
