# Fritzing sketch simon (saved by Fritzing 0.9.3b)
breadboards: 1

parts:
  Part2 = Arduino Uno (Rev3)
  LED1 = LED - 3mm [color="Red (633nm)" package="3 mm [THT]"]
  LED2 = LED - 3mm [color="Yellow (592nm)" package="3 mm [THT]"]
  LED3 = LED - 3mm [color="Green (555nm)" package="3 mm [THT]"]
  LED4 = LED - 3mm [color="Blue (470nm)" package="3 mm [THT]"]
  S1 = Momentary Switch [package=ksa_sealed_tac_switch]
  S2 = Momentary Switch [package=ksa_sealed_tac_switch]
  S3 = Momentary Switch [package=ksa_sealed_tac_switch]
  S4 = Momentary Switch [package=ksa_sealed_tac_switch]
  J1 = Piezo Speaker
  R2 = Resistor [tolerance=±5% resistance=10k package=THT]
  R3 = Resistor [tolerance=±5% resistance=220 package=THT]
  R4 = Resistor [tolerance=±5% resistance=10k package=THT]
  R5 = Resistor [tolerance=±5% resistance=10k package=THT]
  R6 = Resistor [tolerance=±5% resistance=10k package=THT]

nets:
  N1: Part2.D8, S4.3, S4.4, R4.Pin_0
  N2: Part2.D9_PWM, S3.3, S3.4, R2.Pin_0
  N3: Part2.D10_PWM/SS, S2.3, S2.4, R6.Pin_0
  N4: Part2.D11_PWM/MOSI, S1.3, S1.4, R5.Pin_0
  N5: Part2.GND, J1.pin1, R2.Pin_1, R3.Pin_1, R4.Pin_1, R6.Pin_1
  N6: Part2.D2, LED1.anode
  N7: Part2.D3_PWM, LED2.anode
  N8: Part2.D4, LED3.anode
  N9: Part2.D5_PWM, LED4.anode
  N10: Part2.D6_PWM, J1.pin2
  N11: Part2.5V, S1.1, S1.2, S2.1, S2.2, S3.1, S3.2, S4.1, S4.2
  N12: LED1.cathode, LED2.cathode, LED3.cathode, LED4.cathode, R3.Pin_0
