# Fritzing sketch sr04 (saved by Fritzing 0.9.3b)
breadboards: 1

parts:
  Part1 = Arduino Leonardo (Rev3b)
  LCD1 = LCD screen
  R1 = Resistor [tolerance=±5% resistance=220 package="0603 [SMD]"]
  R2 = Resistor [tolerance=±5% resistance=220 package="0603 [SMD]"]
  hc-sr1 = hc-sr04
  J1 = Piezo Speaker

nets:
  N1: Part1.D2/SDA, J1.pin2
  N2: Part1.D3_PWM/SCL, LCD1.DB6
  N3: Part1.D4/A6, LCD1.DB5
  N4: Part1.D5_PWM, LCD1.DB4
  N5: Part1.D6_PWM/A7, LCD1.DB7
  N6: Part1.D7, hc-sr1.Trig
  5V: Part1.5V, LCD1.VDD, R1.Pin_0, hc-sr1.VCC
  N7: Part1.D8/A8, hc-sr1.Echo
  N8: Part1.D11_PWM, LCD1.E
  N9: Part1.D12/A11, LCD1.RS
  GND: Part1.GND, LCD1.VSS, LCD1.R/W, LCD1.LED-, R2.Pin_0, hc-sr1.GND, J1.pin1
  N10: LCD1.V0, R2.Pin_1
  N11: LCD1.LED+, R1.Pin_1
