# Fritzing sketch transistor (saved by Fritzing 0.9.3b)
breadboards: 1

parts:
  Q1 = pnp-Powertransistor [package="TO220 [THT]"]
  R1 = Resistor [tolerance=±5% resistance=220 package="0805 [SMD]"]
  Part1 = Arduino Uno (Rev3) - ICSP
  M1 = DC Motor
  VCC1 = 4 x AAA Battery Mount
  D1 = Diode [package=diode-1n4001]
  R2 = Rotary Potentiometer (Large) [maximum_resistance=100kΩ package=THT]

nets:
  N1: Q1.base, R1.Pin_1
  N2: Q1.collector, M1.pin_2, D1.C
  N3: Q1.emitter, Part1.GND, VCC1.-, R2.leg2
  N4: R1.Pin_0, Part1.D9_PWM
  N5: Part1.A0, R2.wiper
  N6: Part1.5V, R2.leg1
