# Fritzing sketch us_car (saved by Fritzing 0.9.3b)
breadboards: 1

parts:
  Part1 = Arduino Uno (Rev3) - ICSP
  M1 = DC Motor
  VCC1 = 4 x AAA Battery Mount
  IC1 = L293D [package=THT]
  M2 = DC Motor
  S1 = Pushbutton [package="[THT]"]
  hc-sr1 = hc-sr04  # not connected

nets:
  N1: Part1.D9_PWM, IC1.In_2
  N2: Part1.D10_PWM/SS, IC1.In_1
  N3: Part1.D11_PWM/MOSI, IC1.Enable_1
  N4: Part1.D2, S1.Pin_1, S1.Pin_2
  N5: Part1.D4, IC1.In_3
  N6: Part1.D5_PWM, IC1.In_4
  N7: Part1.D6_PWM, IC1.Enable_2
  N8: Part1.5V, IC1.+V
  N9: Part1.GND, VCC1.-, IC1.0V, S1.Pin_3, S1.Pin_4
  N10: M1.pin_1, IC1.Out_1_(_Controlled_by_Enable_1_)
  N11: M1.pin_2, IC1.Out_2_(_Controlled_by_Enable_1_)
  N12: VCC1.+, IC1.+Vmotor
  N13: IC1.Out_3_(_Controlled_by_Enable_2_), M2.pin_2
  N14: IC1.Out_4_(_Controlled_by_Enable_2_), M2.pin_1
